// Logisim project LRU实验.circ as structural Verilog: 2 circuits, main circuit main
module main (
  input  [4:0] \查询的TAG ,
  input  [1:0] in_2,
  input  in_3,
  input  in_4,
  input  in_5,
  output [1:0] out_6
);

  wire and_1_out, and_2_out, and_3_out, and_4_out, and_5_out, and_6_out, clock_1_out, comparator_1_eq,
       comparator_2_eq, comparator_3_eq, d_ff_1_q, d_ff_2_q, d_ff_3_q, nor_1_out, not_1_out;
  wire [0:0] or_2_out, or_3_out;
  wire [1:0] adder_1_out, count_1_out_4, count_2_out_4, count_3_out_4, multiplexer_1_out, multiplexer_2_out,
       multiplexer_3_out, multiplexer_4_out, or_4_out;
  wire [2:0] comparator_6_gt, multiplexer_5_out;
  wire [4:0] register_1_q, register_2_q, register_3_q;

  Clock clock_1 (.out(clock_1_out));
  D_Flip_Flop d_ff_1 (.clk(clock_1_out), .D(or_2_out[0]), .Q(d_ff_1_q));  // open: Qn, preset, en, reset
  D_Flip_Flop d_ff_2 (.clk(clock_1_out), .D(or_3_out[0]), .Q(d_ff_2_q));  // open: Qn, preset, en, reset
  D_Flip_Flop d_ff_3 (.clk(clock_1_out), .D(or_4_out[0]), .Q(d_ff_3_q));  // open: Qn, preset, en, reset
  and and_1 (and_1_out, or_2_out[0], d_ff_1_q);
  and and_2 (and_2_out, or_3_out[0], d_ff_2_q);
  and and_3 (and_3_out, or_4_out[0], d_ff_3_q);
  Multiplexer #(.select(2), .width(2), .disabled(0), .enable("false")) multiplexer_1 (
    .in0(2'b01), .in1(2'b00), .in2(2'b11), .in3(2'b11), .out(multiplexer_1_out), .sel(or_4_out));
  or or_1 (or_4_out[1], and_1_out, and_2_out, and_3_out);
  Multiplexer #(.select(2), .width(2), .disabled(0), .enable("false")) multiplexer_2 (
    .in0(2'b01), .in1(2'b00), .in2(2'b11), .in3(2'b11), .out(multiplexer_2_out),
    .sel({or_4_out[1], or_2_out[0]}));
  Multiplexer #(.select(2), .width(2), .disabled(0), .enable("false")) multiplexer_3 (
    .in0(2'b01), .in1(2'b00), .in2(2'b11), .in3(2'b11), .out(multiplexer_3_out),
    .sel({or_4_out[1], or_3_out[0]}));
  not not_1 (not_1_out, in_5);
  Register #(.width(5)) register_1 (
    .D(\查询的TAG ), .en(or_2_out[0]), .Q(register_1_q), .clk(clock_1_out), .clr(not_1_out));
  Register #(.width(5)) register_2 (
    .D(\查询的TAG ), .en(or_3_out[0]), .Q(register_2_q), .clk(clock_1_out), .clr(not_1_out));
  Register #(.width(5)) register_3 (
    .D(\查询的TAG ), .en(or_4_out[0]), .Q(register_3_q), .clk(clock_1_out), .clr(not_1_out));
  Comparator #(.width(5), .mode("unsigned")) comparator_1 (
    .a(\查询的TAG ), .b(register_1_q), .eq(comparator_1_eq));  // open: gt, lt
  Comparator #(.width(5), .mode("unsigned")) comparator_2 (
    .a(\查询的TAG ), .b(register_2_q), .eq(comparator_2_eq));  // open: gt, lt
  Comparator #(.width(5), .mode("unsigned")) comparator_3 (
    .a(\查询的TAG ), .b(register_3_q), .eq(comparator_3_eq));  // open: gt, lt
  // Probe on count_1_out_4
  count count_1 (.in_1(multiplexer_2_out), .in_3(clock_1_out), .in_2(not_1_out), .out_4(count_1_out_4));
  // Probe on count_2_out_4
  count count_2 (.in_1(multiplexer_3_out), .in_3(clock_1_out), .in_2(not_1_out), .out_4(count_2_out_4));
  count count_3 (.in_1(multiplexer_1_out), .in_3(clock_1_out), .in_2(not_1_out), .out_4(count_3_out_4));
  // Probe on count_3_out_4
  Multiplexer #(.select(2), .width(2), .disabled(0), .enable("false")) multiplexer_4 (
    .in0(2'b00), .in1(adder_1_out), .in3(out_6), .out(multiplexer_4_out), .sel(in_2));  // open: in2
  Comparator #(.width(2), .mode("unsigned")) comparator_4 (
    .a(count_1_out_4), .b(count_2_out_4), .gt(comparator_6_gt[2]));  // open: eq, lt
  Comparator #(.width(2), .mode("unsigned")) comparator_5 (
    .a(count_2_out_4), .b(count_3_out_4), .gt(comparator_6_gt[1]));  // open: eq, lt
  Comparator #(.width(2), .mode("unsigned")) comparator_6 (
    .a(count_3_out_4), .b(count_1_out_4), .gt(comparator_6_gt[0]));  // open: eq, lt
  Register #(.width(2)) register_4 (.D(multiplexer_4_out), .Q(out_6), .clk(in_4), .clr(in_3));  // open: en
  or or_2 (or_2_out[0], comparator_1_eq, and_4_out);
  or or_3 (or_3_out[0], comparator_2_eq, and_5_out);
  or or_4 (or_4_out[0], comparator_3_eq, and_6_out);
  Adder #(.width(2)) adder_1 (.a(out_6), .b(2'b01), .out(adder_1_out));  // open: cin, cout
  Multiplexer #(.select(3), .width(3), .disabled(0)) multiplexer_5 (
    .in0(3'b100), .in1(3'b001), .in2(3'b010), .in3(3'b010), .in4(3'b100), .in5(3'b001), .in6(3'b100),
    .in7(3'b100), .out(multiplexer_5_out), .sel(comparator_6_gt), .en(in_5));
  and and_4 (and_4_out, multiplexer_5_out[2], nor_1_out);
  and and_5 (and_5_out, multiplexer_5_out[1], nor_1_out);
  and and_6 (and_6_out, multiplexer_5_out[0], nor_1_out);
  nor nor_1 (nor_1_out, comparator_1_eq, comparator_2_eq, comparator_3_eq);

  // Notes on the sheet:
  //   最高位要设置位1
  //   0行
  //   1行
  //   2行
  //   三个MUX分别生成ABC三个计数器控制信号
  //   valid+地址4位置
  //   判断是否有slot连续两次EN都为1
  //   三个MUX分别生成计数器控制信号
  //    真值表2
  //   两次同一个slotEN位1，当前slotEN
  //   00：那计数器就要+1.对应控制信号01
  //   01：那计算器就置0，对应控制信号00
  //   10，11: 计数器保持不变，输出控制信号11
  //   记录TAG
  //   A
  //   B
  //   C
  //   A
  //   B
  //   C
  //   计数器
  //   分别判断ABC内的tag是否有命中的
  //   B和C
  //   分别输出保存TAG寄存器的EN
  //   A和B比较
  //   C和A比较
  //   不管更新还是命中TAG，对应计数器都要设置位0
  //   如果同一个slot连续命中，那其他slot的计数器就不变。
  //   某个slot的EN为1的情况：1 该slot命中（命中时也做一次无意义的对TAG的更新），2替换，替换发生在没有任何一个命中，并且某个slot被选中替换时
  //   情况1
  //   情况2
  //   对应一个真值表
  //   000，111：输出100，表示选择A被替换
  //   001，101：输出001，表示选择C被替换
  //   这一部分决定
  //   如果替换，替换谁
  //   :010或011:输出是010，表示选择B被替换
  //   100,110输出100，表示选择A替换
  //   只要有1个命中输出0
endmodule

module count (
  input  [1:0] in_1,
  input  in_2,
  input  in_3,
  output [1:0] out_4
);

  wire [1:0] adder_1_out, multiplexer_1_out;

  Multiplexer #(.select(2), .width(2), .disabled(0), .enable("false")) multiplexer_1 (
    .in0(2'b00), .in1(adder_1_out), .in3(out_4), .out(multiplexer_1_out), .sel(in_1));  // open: in2
  Register #(.width(2)) register_1 (.D(multiplexer_1_out), .Q(out_4), .clk(in_3), .clr(in_2));  // open: en
  Adder #(.width(2)) adder_1 (.a(out_4), .b(2'b01), .out(adder_1_out));  // open: cin, cout

  // Notes on the sheet:
  //   控制端
  //   控制端00：置0
  //    01：每来一个上升沿+1
  //   11：保持不变
  //   时钟
  //   1时直接清零
endmodule
