// Logisim project RAM读写操作实验.circ as structural Verilog: 1 circuit, main circuit main
module main (
  input  [2:0] \三位地址线 ,
  input  [7:0] \要写入的数据 ,
  input  in_3,
  input  \_0写1读 ,
  output [7:0] \读出的数据 
);

  wire clock_1_out, not_1_out;
  wire [7:0] ram_1_data;

  Clock clock_1 (.out(clock_1_out));
  RAM #(.addrWidth(3)) ram_1 (
    .addr(\三位地址线 ), .data(ram_1_data), .sel(1'b1), .clk(clock_1_out), .ld(\_0写1读 ), .clr(in_3));
  assign \读出的数据  = \_0写1读  ? ram_1_data : 8'bz;  // Controlled_Buffer controlled_buffer_1
  assign ram_1_data = not_1_out ? \要写入的数据  : 8'bz;  // Controlled_Buffer controlled_buffer_2
  not not_1 (not_1_out, \_0写1读 );

  // Notes on the sheet:
  //   读写操作实验
  //   读的时候只要给好地址，ld设置为1，直接读出
  //   写的时候要给好地址，给好要写的数据，ld设置为0，然后等待上升沿到来，才能写入
endmodule
