// Logisim project cache全相联映射实验.circ as structural Verilog: 1 circuit, main circuit main
module main (
  input  [5:0] \块地址 ,
  input  [1:0] \块内地址 ,
  output [7:0] out_3,
  output out_4
);

  wire clock_1_out, comparator_1_eq, comparator_2_eq, comparator_3_eq, comparator_4_eq;
  wire [1:0] priority_encoder_1_out;
  wire [5:0] register_1_q, register_2_q, register_3_q, register_4_q;
  wire [7:0] ram_1_data;

  Clock clock_1 (.out(clock_1_out));
  Register #(.width(6)) register_1 (.Q(register_1_q), .clk(clock_1_out));  // open: D, en, clr
  Register #(.width(6)) register_2 (.Q(register_2_q), .clk(clock_1_out));  // open: D, en, clr
  Register #(.width(6)) register_3 (.Q(register_3_q), .clk(clock_1_out));  // open: D, en, clr
  Register #(.width(6)) register_4 (.Q(register_4_q), .clk(clock_1_out));  // open: D, en, clr
  Comparator #(.width(6), .mode("unsigned")) comparator_1 (
    .a(register_1_q), .b(\块地址 ), .eq(comparator_1_eq));  // open: gt, lt
  Comparator #(.width(6), .mode("unsigned")) comparator_2 (
    .a(register_2_q), .b(\块地址 ), .eq(comparator_2_eq));  // open: gt, lt
  Comparator #(.width(6), .mode("unsigned")) comparator_3 (
    .a(register_3_q), .b(\块地址 ), .eq(comparator_3_eq));  // open: gt, lt
  Comparator #(.width(6), .mode("unsigned")) comparator_4 (
    .a(register_4_q), .b(\块地址 ), .eq(comparator_4_eq));  // open: gt, lt
  Priority_Encoder #(.select(2)) priority_encoder_1 (
    .in0(comparator_1_eq), .in1(comparator_2_eq), .in2(comparator_3_eq), .in3(comparator_4_eq),
    .out(priority_encoder_1_out), .gs(out_4));  // open: en_out, en_in
  RAM #(.addrWidth(4)) ram_1 (
    .addr({priority_encoder_1_out, \块内地址 }), .data(ram_1_data), .sel(1'b1), .clk(clock_1_out), .ld(out_4),
    .clr(1'b0));
  assign out_3 = out_4 ? ram_1_data : 8'bz;  // Controlled_Buffer controlled_buffer_1

  // Notes on the sheet:
  //   (TAG）
  //   要初始化4个TAG，要不相同
  //   全相联映射实验，主存地址8位，块内地址2位，cache的line地址2位置（4个cache line）
  //   line0
  //   line1
  //   TAG
  //   line2
  //   line3
  //   TAG
  //   TAG
  //   TAG
  //   不考虑写，替换
  //   如果有一个块命中，则通过编码器得到对应line号
  //   date，根据line号（高2位）和块内地址（低2位）构成的cache地址读取
  //   如果没有一个块命中，ld会位0，这时候不会读取
endmodule
