// Logisim project cache直接映射实验.circ as structural Verilog: 1 circuit, main circuit main
module main (
  input  [3:0] \cache_line号 ,
  input  [1:0] \块内地址 ,
  input  [1:0] in_3,
  output [7:0] out_4
);

  wire clock_1_out, comparator_1_eq;
  wire [3:0] ram_1_data;
  wire [7:0] ram_2_data;

  Clock clock_1 (.out(clock_1_out));
  Comparator #(.width(4)) comparator_1 (.a(\cache_line号 ), .b(ram_1_data), .eq(comparator_1_eq));  // open: gt, lt
  RAM #(.addrWidth(2), .dataWidth(4)) ram_1 (
    .addr(\块内地址 ), .data(ram_1_data), .sel(1'b1), .clk(clock_1_out), .ld(1'b1), .clr(1'b0));
  RAM #(.addrWidth(4)) ram_2 (
    .addr({\块内地址 , in_3}), .data(ram_2_data), .sel(1'b1), .clk(clock_1_out), .ld(comparator_1_eq), .clr(1'b0));
  assign out_4 = comparator_1_eq ? ram_2_data : 8'bz;  // Controlled_Buffer controlled_buffer_1

  // Notes on the sheet:
  //   TAG
  //   6位block号
  //   主存地址8位
  //   直接映射：把要查询主存地址分为3部分，这里不考虑cache有效位
  //   一开始要初始化TAG，要不同
  //   记录TAG
  //   cache有4line，每个块4个单元
  //   如果TAG匹配则读date
  //   根据line号以及块内地址构成的4位cache地址读date内容
endmodule
