// Logisim project 原码1位乘法器.circ as structural Verilog: 1 circuit, main circuit main
module main (
  input  [3:0] \STEP1_输入A小数部分 ,
  input  [3:0] \STEP2_输入B小数部分 ,
  input  in_3,
  input  A0,
  input  B0,
  output S0,
  output [7:0] \数值位 
);

  wire adder_2_cout, clock_1_out, d_ff_1_q, multiplexer_1_out, multiplexer_2_out, multiplexer_3_out,
       multiplexer_4_out, multiplexer_5_out, multiplexer_6_out, multiplexer_9_out, multiplexer_10_out,
       multiplexer_11_out;
  wire [0:0] comparator_1_eq;
  wire [1:0] multiplexer_12_out, register_2_q;
  wire [3:0] adder_1_out, adder_2_out, multiplexer_7_out, multiplexer_8_out, register_1_q;

  Clock clock_1 (.out(clock_1_out));
  Multiplexer #(.select(2), .disabled(0), .enable("false")) multiplexer_1 (
    .in0(1'b0), .in1(adder_2_cout), .in2(1'b0), .in3(d_ff_1_q), .out(multiplexer_1_out), .sel(register_2_q));
  Multiplexer #(.select(2), .disabled(0), .enable("false")) multiplexer_2 (
    .in0(\STEP2_输入B小数部分 [3]), .in1(\数值位 [3]), .in2(\数值位 [4]), .in3(\数值位 [3]), .out(multiplexer_2_out),
    .sel(register_2_q));
  D_Flip_Flop d_ff_1 (.clk(clock_1_out), .D(multiplexer_1_out), .Q(d_ff_1_q), .reset(in_3));  // open: Qn, preset, en
  D_Flip_Flop d_ff_2 (.clk(clock_1_out), .D(multiplexer_2_out), .Q(\数值位 [3]));  // open: Qn, preset, en, reset
  Multiplexer #(.select(2), .disabled(0), .enable("false")) multiplexer_3 (
    .in0(1'b0), .in1(adder_2_out[3]), .in2(d_ff_1_q), .in3(\数值位 [7]), .out(multiplexer_3_out),
    .sel(register_2_q));
  Multiplexer #(.select(2), .disabled(0), .enable("false")) multiplexer_4 (
    .in0(\STEP2_输入B小数部分 [2]), .in1(\数值位 [2]), .in2(\数值位 [3]), .in3(\数值位 [2]), .out(multiplexer_4_out),
    .sel(register_2_q));
  Adder #(.width(4)) adder_1 (.a(register_1_q), .b(4'b0001), .out(adder_1_out));  // open: cin, cout
  D_Flip_Flop d_ff_3 (.clk(clock_1_out), .D(multiplexer_3_out), .Q(\数值位 [7]), .reset(in_3));  // open: Qn, preset, en
  D_Flip_Flop d_ff_4 (.clk(clock_1_out), .D(multiplexer_4_out), .Q(\数值位 [2]));  // open: Qn, preset, en, reset
  Multiplexer #(.select(2), .disabled(0), .enable("false")) multiplexer_5 (
    .in0(1'b0), .in1(adder_2_out[2]), .in2(\数值位 [7]), .in3(\数值位 [6]), .out(multiplexer_5_out),
    .sel(register_2_q));
  Multiplexer #(.select(2), .disabled(0), .enable("false")) multiplexer_6 (
    .in0(\STEP2_输入B小数部分 [1]), .in1(\数值位 [1]), .in2(\数值位 [2]), .in3(\数值位 [1]), .out(multiplexer_6_out),
    .sel(register_2_q));
  Register #(.width(4)) register_1 (
    .D(multiplexer_7_out), .Q(register_1_q), .clk(clock_1_out), .clr(in_3));  // open: en
  Multiplexer #(.select(2), .width(4), .disabled(0), .enable("false")) multiplexer_7 (
    .in0(register_1_q), .in1(register_1_q), .in2(adder_1_out), .in3(register_1_q), .out(multiplexer_7_out),
    .sel(register_2_q));
  Multiplexer #(.width(4), .disabled(0), .enable("false")) multiplexer_8 (
    .in0(4'b0000), .in1(\STEP1_输入A小数部分 ), .out(multiplexer_8_out), .sel(\数值位 [0]));
  D_Flip_Flop d_ff_5 (.clk(clock_1_out), .D(multiplexer_5_out), .Q(\数值位 [6]), .reset(in_3));  // open: Qn, preset, en
  D_Flip_Flop d_ff_6 (.clk(clock_1_out), .D(multiplexer_6_out), .Q(\数值位 [1]));  // open: Qn, preset, en, reset
  Adder #(.width(4)) adder_2 (
    .a(\数值位 [7:4]), .b(multiplexer_8_out), .out(adder_2_out), .cout(adder_2_cout));  // open: cin
  Multiplexer #(.select(2), .disabled(0), .enable("false")) multiplexer_9 (
    .in0(1'b0), .in1(adder_2_out[1]), .in2(\数值位 [6]), .in3(\数值位 [5]), .out(multiplexer_9_out),
    .sel(register_2_q));
  Multiplexer #(.select(2), .disabled(0), .enable("false")) multiplexer_10 (
    .in0(\STEP2_输入B小数部分 [0]), .in1(\数值位 [0]), .in2(\数值位 [1]), .in3(\数值位 [0]), .out(multiplexer_10_out),
    .sel(register_2_q));
  Comparator #(.width(4), .mode("unsigned")) comparator_1 (
    .a(register_1_q), .b(4'b0011), .eq(comparator_1_eq[0]));  // open: gt, lt
  D_Flip_Flop d_ff_7 (.clk(clock_1_out), .D(multiplexer_9_out), .Q(\数值位 [5]), .reset(in_3));  // open: Qn, preset, en
  D_Flip_Flop d_ff_8 (.clk(clock_1_out), .D(multiplexer_10_out), .Q(\数值位 [0]));  // open: Qn, preset, en, reset
  Multiplexer #(.select(2), .disabled(0), .enable("false")) multiplexer_11 (
    .in0(1'b0), .in1(adder_2_out[0]), .in2(\数值位 [5]), .in3(\数值位 [4]), .out(multiplexer_11_out),
    .sel(register_2_q));
  xor xor_1 (S0, A0, B0);
  D_Flip_Flop d_ff_9 (.clk(clock_1_out), .D(multiplexer_11_out), .Q(\数值位 [4]), .reset(in_3));  // open: Qn, preset, en
  // Probe on multiplexer_12_out
  Multiplexer #(.select(3), .width(2), .disabled(0), .enable("false")) multiplexer_12 (
    .in0(2'b01), .in1(2'b00), .in2(2'b10), .in3(2'b10), .in4(2'b01), .in5(2'b11), .in6(2'b11), .in7(2'b11),
    .out(multiplexer_12_out), .sel({register_2_q, comparator_1_eq[0]}));
  Register #(.width(2)) register_2 (
    .D(multiplexer_12_out), .Q(register_2_q), .clk(clock_1_out), .clr(in_3));  // open: en
  // Probe on register_2_q

  // Notes on the sheet:
  //   A1A2A3A4
  //   B1B2B3B4
  //   STEP4不停的点击时钟，观测原码1位乘法结果
  //   STEP3这里点1，然后点0，完成计数器、状态reg以及部分积初始化
  //   原码A0.A1A2A3A4*原码B0.B1B2B3B4
  //   进位信号
  //   B1
  //   当状态10时，计数器的次态+1
  //   部分积
  //   B2
  //   初始计数是0
  //   根据B4决定是加被乘数还是0
  //   B3
  //   从0到N-1
  //   B4
  //   次态逻辑
  //   当状态00和11时保持不变，状态为01时把加后结果更新部分积，为10时右移1次
  //   符号位
  //   状态reg
  //   N=4.一共进行4轮01-10
  //   四个状态
  //   11：结束状态
  //   00->01>10->01->10->01->10->01->10->11
  //   01：做加法运算，下一个状态进入10态
  //   00：设置部分积次态为0000，B1B2B3B4的次态为乘数小数部分，下一个周期进入01态
  //   10：做移位运算，如果当前计数不等于3（N-1），则回到01态，否则进入11态
endmodule
