// Logisim project 存储器扩展实验.circ as structural Verilog: 1 circuit, main circuit main
module main (
  input  [3:0] \地址高两位做字扩展片选 ,
  input  in_2,
  output [7:0] \读出的数据_本实验只考虑读 
);

  wire clock_1_out, decoder_1_out0, decoder_1_out1, decoder_1_out2, decoder_1_out3;

  Decoder #(.select(2), .disabled(0)) decoder_1 (
    .out0(decoder_1_out0), .out1(decoder_1_out1), .out2(decoder_1_out2), .out3(decoder_1_out3),
    .sel(\地址高两位做字扩展片选 [3:2]), .en(in_2));
  Clock clock_1 (.out(clock_1_out));
  RAM #(.addrWidth(2), .dataWidth(4)) ram_1 (
    .addr(\地址高两位做字扩展片选 [1:0]), .data(\读出的数据_本实验只考虑读 [7:4]), .sel(decoder_1_out0), .clk(clock_1_out),
    .ld(1'b1), .clr(1'b0));
  RAM #(.addrWidth(2), .dataWidth(4)) ram_2 (
    .addr(\地址高两位做字扩展片选 [1:0]), .data(\读出的数据_本实验只考虑读 [7:4]), .sel(decoder_1_out1), .clk(clock_1_out),
    .ld(1'b1), .clr(1'b0));
  RAM #(.addrWidth(2), .dataWidth(4)) ram_3 (
    .addr(\地址高两位做字扩展片选 [1:0]), .data(\读出的数据_本实验只考虑读 [7:4]), .sel(decoder_1_out2), .clk(clock_1_out),
    .ld(1'b1), .clr(1'b0));
  RAM #(.addrWidth(2), .dataWidth(4)) ram_4 (
    .addr(\地址高两位做字扩展片选 [1:0]), .data(\读出的数据_本实验只考虑读 [7:4]), .sel(decoder_1_out3), .clk(clock_1_out),
    .ld(1'b1), .clr(1'b0));
  RAM #(.addrWidth(2), .dataWidth(4)) ram_5 (
    .addr(\地址高两位做字扩展片选 [1:0]), .data(\读出的数据_本实验只考虑读 [3:0]), .sel(decoder_1_out0), .clk(clock_1_out),
    .ld(1'b1), .clr(1'b0));
  RAM #(.addrWidth(2), .dataWidth(4)) ram_6 (
    .addr(\地址高两位做字扩展片选 [1:0]), .data(\读出的数据_本实验只考虑读 [3:0]), .sel(decoder_1_out1), .clk(clock_1_out),
    .ld(1'b1), .clr(1'b0));
  RAM #(.addrWidth(2), .dataWidth(4)) ram_7 (
    .addr(\地址高两位做字扩展片选 [1:0]), .data(\读出的数据_本实验只考虑读 [3:0]), .sel(decoder_1_out2), .clk(clock_1_out),
    .ld(1'b1), .clr(1'b0));
  RAM #(.addrWidth(2), .dataWidth(4)) ram_8 (
    .addr(\地址高两位做字扩展片选 [1:0]), .data(\读出的数据_本实验只考虑读 [3:0]), .sel(decoder_1_out3), .clk(clock_1_out),
    .ld(1'b1), .clr(1'b0));

  // Notes on the sheet:
  //   为0时，所有都不选择
  //   地址低两位并联所有的片内地址
  //   行方向做位扩展
  //   同一行的sel并联
  //   数据高4位，和低4拼接
  //   列方向做字扩展
  //   地址0-3位扩展
  //   地址4-7位扩展
  //   地址8-11位扩展
  //   地址12-15位扩展
  //   低4位数据
endmodule
