// Logisim project 微操作实验.circ as structural Verilog: 2 circuits, main circuit main
module main (
  input  \复位 ,
  input  IRi,
  input  IRo,
  input  PCi,
  input  PCo,
  input  PC_1,
  input  MARi,
  input  W_R,
  input  MDRi,
  input  MDRo,
  input  R0i,
  input  R0o,
  input  R1i,
  input  R1o,
  input  R2i,
  input  R2o,
  input  R3i,
  input  R3o,
  input  Yi,
  input  Xi,
  input  [1:0] ALUop,
  input  ALUo,
  input  G
);

  wire not_1_out, not_2_out, ZF, \时钟_out ;
  wire [7:0] A_q, adder_1_out, alu_1_aluresult, B_q, controlled_buffer_1_out, controlled_buffer_3_out,
       controlled_buffer_4_out, controlled_buffer_7_out, controlled_buffer_9_out, controlled_buffer_11_out,
       controlled_buffer_14_out, controlled_buffer_15_out, G_out, IR_q, IRi_out, MAR_q, MDR_q,
       multiplexer_1_out, multiplexer_2_out, multiplexer_3_out, PC_q, R0_q, R1_q, R2_q, R3_q, R3i_out,
       ram_1_data;

  Clock \u_时钟  (.out(\时钟_out ));
  assign IRi_out = IRi ? G_out : 8'bz;  // Controlled_Buffer IRi
  Multiplexer #(.width(8), .disabled(0), .enable("false")) multiplexer_1 (
    .in0(multiplexer_2_out), .in1(G_out), .out(multiplexer_1_out), .sel(PCi));
  Register IR (.D(IRi_out), .Q(IR_q), .clk(\时钟_out ), .clr(\复位 ));  // open: en
  assign controlled_buffer_1_out = IRo ? IR_q : 8'bz;  // Controlled_Buffer controlled_buffer_1
  Register PC (.D(multiplexer_1_out), .Q(PC_q), .clk(\时钟_out ), .clr(\复位 ));  // open: en
  assign controlled_buffer_1_out = PCo ? PC_q : 8'bz;  // Controlled_Buffer controlled_buffer_2
  Multiplexer #(.width(8), .disabled(0), .enable("false")) multiplexer_2 (
    .in0(PC_q), .in1(adder_1_out), .out(multiplexer_2_out), .sel(PC_1));
  Adder adder_1 (.a(8'h1), .b(PC_q), .out(adder_1_out));  // open: cin, cout
  assign controlled_buffer_3_out = MARi ? G_out : 8'bz;  // Controlled_Buffer controlled_buffer_3
  Register MAR (.D(controlled_buffer_3_out), .Q(MAR_q), .clk(\时钟_out ), .clr(\复位 ));  // open: en
  RAM #(.bus("asynch")) ram_1 (.addr(MAR_q), .data(ram_1_data), .ld(not_1_out));  // open: sel, clr
  not not_1 (not_1_out, W_R);
  assign controlled_buffer_4_out = not_1_out ? ram_1_data : 8'bz;  // Controlled_Buffer controlled_buffer_4
  Multiplexer #(.width(8), .disabled(0), .enable("false")) multiplexer_3 (
    .in0(controlled_buffer_4_out), .in1(G_out), .out(multiplexer_3_out), .sel(MDRi));
  assign ram_1_data = not_2_out ? MDR_q : 8'bz;  // Controlled_Buffer controlled_buffer_5
  not not_2 (not_2_out, not_1_out);
  Register MDR (.D(multiplexer_3_out), .Q(MDR_q), .clk(\时钟_out ), .clr(\复位 ));  // open: en
  assign controlled_buffer_1_out = MDRo ? MDR_q : 8'bz;  // Controlled_Buffer controlled_buffer_6
  assign controlled_buffer_7_out = R0i ? G_out : 8'bz;  // Controlled_Buffer controlled_buffer_7
  Register R0 (.D(controlled_buffer_7_out), .Q(R0_q), .clk(\时钟_out ), .clr(\复位 ));  // open: en
  assign controlled_buffer_1_out = R0o ? R0_q : 8'bz;  // Controlled_Buffer controlled_buffer_8
  assign controlled_buffer_9_out = R1i ? G_out : 8'bz;  // Controlled_Buffer controlled_buffer_9
  Register R1 (.D(controlled_buffer_9_out), .Q(R1_q), .clk(\时钟_out ), .clr(\复位 ));  // open: en
  assign controlled_buffer_1_out = R1o ? R1_q : 8'bz;  // Controlled_Buffer controlled_buffer_10
  assign controlled_buffer_11_out = R2i ? G_out : 8'bz;  // Controlled_Buffer controlled_buffer_11
  assign R3i_out = R3i ? G_out : 8'bz;  // Controlled_Buffer R3i
  Register R2 (.D(controlled_buffer_11_out), .Q(R2_q), .clk(\时钟_out ), .clr(\复位 ));  // open: en
  assign controlled_buffer_1_out = R2o ? R2_q : 8'bz;  // Controlled_Buffer controlled_buffer_12
  Register R3 (.D(R3i_out), .Q(R3_q), .clk(\时钟_out ), .clr(\复位 ));  // open: en
  assign controlled_buffer_1_out = R3o ? R3_q : 8'bz;  // Controlled_Buffer controlled_buffer_13
  assign controlled_buffer_14_out = Xi ? G_out : 8'bz;  // Controlled_Buffer controlled_buffer_14
  assign controlled_buffer_15_out = Yi ? G_out : 8'bz;  // Controlled_Buffer controlled_buffer_15
  Register A (.D(controlled_buffer_14_out), .Q(A_q), .clk(\时钟_out ), .clr(\复位 ));  // open: en
  Register B (.D(controlled_buffer_15_out), .Q(B_q), .clk(\时钟_out ), .clr(\复位 ));  // open: en
  // Probe on alu_1_aluresult
  ALU alu_1 (.A(A_q), .B(B_q), .ALUop(ALUop), .ALUresult(alu_1_aluresult), .ZF(ZF));
  assign controlled_buffer_1_out = ALUo ? alu_1_aluresult : 8'bz;  // Controlled_Buffer controlled_buffer_16
  assign G_out = G ? controlled_buffer_1_out : 8'bz;  // Controlled_Buffer G

  // Notes on the sheet:
  //   步骤2：输入完所有控制信号
  //   步骤3：使时钟产生一个上升沿脉冲
  //   重复步骤2到步骤3
  //   步骤1：设置复位为1后再设置复位为0
  //   指令举例：
  //   ADD R1,R2
  //   SUB R1,R2
  //   ST 01000
  //   LD 01000
  //   JE 01000
  //   MOV R0,R1
  //   ADDI 01000
  //   对应机器指令
  //   000-01-02-0
  //   001-01-02-0
  //   010-01000
  //   将R0内容存入，MEM[(R1)+01000]，默认使用R0和R1
  //   期中此时R1为基地寄存器，01000为偏移量，这是5位补码
  //   后面机器指令中的立即数都为5位补码
  //   011-01000
  //   将MEM[(R1)+01000]内容送入R0，默认使用R0和R1
  //   100-01000
  //   判断R0是否为0，为0则设置PC为 PC+1+01000 
  //   101-00-01-0
  //   110-01000
  //   (R2)+(R1)->R2
  //   由于机器指令8位，寄存器编码是2位表示1个寄存器，因此第0位这里设置为0
  //   (R2)-(R1)->R2
  //   (R1)->R0
  //   （R1）+01000->R1
  //   默认源寄存器和目的寄存器R1
  //   存储器RAM
  //   手动输入控制信号
  //    000,RB,RA,*
  //   001,RB,RA,*
  //   010,*****
  //   011,*****
  //   100,*****
  //   操作码3位,机器码8位 
  //   (RA)+(RB)->RA
  //   (RA)-(RB)->RA
  //   101,RB,RA,  (RA)->RB
  //   110 ***,将***加到R1上
  //   将R0里的内容存入内存(R1)+*****
  //   将内存地址（R1)+*****里内容给R0
  //   判断R0内容是否为0，如果是0，则将PC更改为（PC)+1+*****
endmodule

module ALU (
  input  [7:0] A,
  input  [7:0] B,
  input  [1:0] ALUop,
  output [7:0] ALUresult,
  output ZF
);

  wire [7:0] adder_1_out, adder_2_out, bit_extender_1_out, subtractor_1_out;

  Adder adder_1 (.a(A), .b(B), .out(adder_1_out));  // open: cin, cout
  Subtractor subtractor_1 (.a(A), .b(B), .out(subtractor_1_out));  // open: bin, bout
  assign bit_extender_1_out = {{3{B[4]}}, B[4:0]};  // Bit_Extender bit_extender_1
  Comparator comparator_1 (.a(A), .b({8{1'b0}}), .eq(ZF));  // open: gt, lt
  Adder adder_2 (.a(A), .b(bit_extender_1_out), .out(adder_2_out));  // open: cin, cout
  Multiplexer #(.select(2), .width(8), .disabled(0), .enable("false")) multiplexer_1 (
    .in0(adder_1_out), .in1(subtractor_1_out), .in2(adder_2_out), .in3(A), .out(ALUresult), .sel(ALUop));

  // Notes on the sheet:
  //   ALUop,00A+B,01A-B.10A+立即数5位有符号扩展,11输出A
endmodule
