// Logisim project 微程序控制器实验.circ as structural Verilog: 2 circuits, main circuit main
module main (
  input  \复位 ,
  input  \手动 ,
  input  in_3,
  input  in_4,
  input  in_5,
  input  in_6,
  input  in_7,
  input  in_8,
  input  in_9,
  input  in_10,
  input  in_11,
  input  in_12,
  input  in_13,
  input  in_14,
  input  in_15,
  input  in_16,
  input  in_17,
  input  in_18,
  input  in_19,
  input  in_20,
  input  in_21,
  input  [1:0] in_22,
  input  in_23,
  input  in_24
);

  wire ALUo, CLK, controlled_buffer_1_out, controlled_buffer_2_out, controlled_buffer_6_out,
       controlled_buffer_7_out, controlled_buffer_11_out, controlled_buffer_14_out, controlled_buffer_16_out,
       controlled_buffer_20_out, controlled_buffer_21_out, controlled_buffer_24_out,
       controlled_buffer_29_out, controlled_buffer_30_out, controlled_buffer_34_out,
       controlled_buffer_38_out, controlled_buffer_39_out, controlled_buffer_43_out,
       controlled_buffer_44_out, controlled_buffer_47_out, controlled_buffer_52_out,
       controlled_buffer_57_out, controlled_buffer_58_out, G, IRi, IRo, MARi, MDRi, MDRo, not_1_out,
       not_2_out, not_3_out, PC_1, PCi, PCo, R0i, R0o, R1i, R1o, R2i, R2o, R3i, R3o, W_R, Xi, Yi, ZF;
  wire [1:0] ALUop, controlled_buffer_54_out, multiplexer_6_out;
  wire [5:0] adder_2_out, multiplexer_2_out, multiplexer_4_out, multiplexer_5_out, multiplexer_7_out,
       register_1_q;
  wire [7:0] A_q, adder_1_out, alu_1_aluresult, B_q, controlled_buffer_5_out, controlled_buffer_13_out,
       controlled_buffer_18_out, controlled_buffer_27_out, controlled_buffer_32_out,
       controlled_buffer_37_out, controlled_buffer_50_out, controlled_buffer_51_out, G_out, Instr, IRi_out,
       MAR_q, MDR_q, multiplexer_1_out, multiplexer_3_out, multiplexer_8_out, PC_q, R0_q, R1_q, R2_q, R3_q,
       R3i_out, ram_1_data;
  wire [14:0] rom_1_data;

  Clock \u_时钟  (.out(CLK));
  assign controlled_buffer_1_out = \手动  ? in_3 : 1'bz;  // Controlled_Buffer controlled_buffer_1
  not not_1 (not_1_out, \手动 );
  assign IRi_out = controlled_buffer_1_out ? G_out : 8'bz;  // Controlled_Buffer IRi
  assign controlled_buffer_2_out = \手动  ? in_4 : 1'bz;  // Controlled_Buffer controlled_buffer_2
  assign controlled_buffer_1_out = not_1_out ? IRi : 1'bz;  // Controlled_Buffer controlled_buffer_3
  assign controlled_buffer_2_out = not_1_out ? IRo : 1'bz;  // Controlled_Buffer controlled_buffer_4
  // Probe on IRo
  // Probe on IRi
  Multiplexer #(.width(8), .disabled(0), .enable("false")) multiplexer_1 (
    .in0(multiplexer_3_out), .in1(G_out), .out(multiplexer_1_out), .sel(controlled_buffer_6_out));
  Register IR (.D(IRi_out), .Q(Instr), .clk(CLK), .clr(\复位 ));  // open: en
  assign controlled_buffer_5_out = controlled_buffer_2_out ? Instr : 8'bz;  // Controlled_Buffer controlled_buffer_5
  assign controlled_buffer_6_out = \手动  ? in_5 : 1'bz;  // Controlled_Buffer controlled_buffer_6
  assign controlled_buffer_7_out = \手动  ? in_6 : 1'bz;  // Controlled_Buffer controlled_buffer_7
  assign controlled_buffer_6_out = not_1_out ? PCi : 1'bz;  // Controlled_Buffer controlled_buffer_8
  // Probe on PCi
  Register PC (.D(multiplexer_1_out), .Q(PC_q), .clk(CLK), .clr(\复位 ));  // open: en
  assign controlled_buffer_5_out = controlled_buffer_7_out ? PC_q : 8'bz;  // Controlled_Buffer controlled_buffer_9
  assign controlled_buffer_7_out = not_1_out ? PCo : 1'bz;  // Controlled_Buffer controlled_buffer_10
  // Probe on PCo
  Multiplexer #(.width(6), .disabled(0), .enable("false")) multiplexer_2 (
    .in0({6{1'b0}}), .in1(adder_2_out), .out(multiplexer_2_out), .sel(ZF));
  Multiplexer #(.width(8), .disabled(0), .enable("false")) multiplexer_3 (
    .in0(PC_q), .in1(adder_1_out), .out(multiplexer_3_out), .sel(controlled_buffer_11_out));
  Adder adder_1 (.a(8'h1), .b(PC_q), .out(adder_1_out));  // open: cin, cout
  assign controlled_buffer_11_out = \手动  ? in_7 : 1'bz;  // Controlled_Buffer controlled_buffer_11
  assign controlled_buffer_11_out = not_1_out ? PC_1 : 1'bz;  // Controlled_Buffer controlled_buffer_12
  // Probe on PC_1
  Multiplexer #(.select(3), .width(6), .disabled(0), .enable("false")) multiplexer_4 (
    .in0(adder_2_out), .in1(adder_2_out), .in2(adder_2_out), .in3(adder_2_out), .in4(multiplexer_2_out),
    .in5(adder_2_out), .in6(adder_2_out), .in7(adder_2_out), .out(multiplexer_4_out), .sel(Instr[7:5]));
  assign controlled_buffer_13_out = controlled_buffer_14_out ? G_out : 8'bz;  // Controlled_Buffer controlled_buffer_13
  assign controlled_buffer_14_out = \手动  ? in_8 : 1'bz;  // Controlled_Buffer controlled_buffer_14
  assign controlled_buffer_14_out = not_1_out ? MARi : 1'bz;  // Controlled_Buffer controlled_buffer_15
  // Probe on MARi
  Multiplexer #(.select(3), .width(6), .disabled(0), .enable("false")) multiplexer_5 (
    .in0(6'b000100), .in1(6'b001000), .in2(6'b001100), .in3(6'b010100), .in4(6'b011100), .in5(6'b100100),
    .in6(6'b101000), .out(multiplexer_5_out), .sel(Instr[7:5]));  // open: in7
  Register MAR (.D(controlled_buffer_13_out), .Q(MAR_q), .clk(CLK), .clr(\复位 ));  // open: en
  Adder #(.width(6)) adder_2 (.a(register_1_q), .b(6'b000001), .out(adder_2_out));  // open: cin, cout
  RAM #(.bus("asynch")) ram_1 (.addr(MAR_q), .data(ram_1_data), .ld(not_2_out));  // open: sel, clr
  not not_2 (not_2_out, controlled_buffer_16_out);
  assign controlled_buffer_16_out = \手动  ? in_9 : 1'bz;  // Controlled_Buffer controlled_buffer_16
  assign controlled_buffer_16_out = not_1_out ? W_R : 1'bz;  // Controlled_Buffer controlled_buffer_17
  // Probe on W_R
  assign controlled_buffer_18_out = not_2_out ? ram_1_data : 8'bz;  // Controlled_Buffer controlled_buffer_18
  Decoder #(.select(2), .disabled(0)) decoder_1 (
    .out0(R0i), .out1(R1i), .out2(R2i), .out3(R3i), .sel(multiplexer_6_out), .en(rom_1_data[14]));
  Multiplexer #(.select(2), .width(2), .disabled(0), .enable("false")) multiplexer_6 (
    .in0(2'b00), .in1(2'b01), .in2(Instr[2:1]), .in3(Instr[4:3]), .out(multiplexer_6_out),
    .sel(rom_1_data[3:2]));
  Multiplexer #(.select(3), .width(6), .disabled(0), .enable("false")) multiplexer_7 (
    .in0(adder_2_out), .in1({6{1'b0}}), .in2(multiplexer_4_out), .in3({6{1'b0}}), .in4(multiplexer_5_out),
    .in5({6{1'b0}}), .in6({6{1'b0}}), .in7({6{1'b0}}), .out(multiplexer_7_out), .sel(rom_1_data[6:4]));
  Register #(.width(6)) register_1 (.D(multiplexer_7_out), .Q(register_1_q), .clk(CLK), .clr(\复位 ));  // open: en
  Multiplexer #(.width(8), .disabled(0), .enable("false")) multiplexer_8 (
    .in0(controlled_buffer_18_out), .in1(G_out), .out(multiplexer_8_out), .sel(controlled_buffer_20_out));
  assign ram_1_data = not_3_out ? MDR_q : 8'bz;  // Controlled_Buffer controlled_buffer_19
  not not_3 (not_3_out, not_2_out);
  assign controlled_buffer_20_out = \手动  ? in_10 : 1'bz;  // Controlled_Buffer controlled_buffer_20
  assign controlled_buffer_21_out = \手动  ? in_11 : 1'bz;  // Controlled_Buffer controlled_buffer_21
  assign controlled_buffer_20_out = not_1_out ? MDRi : 1'bz;  // Controlled_Buffer controlled_buffer_22
  // Probe on MDRi
  // Probe on MDRo
  Register MDR (.D(multiplexer_8_out), .Q(MDR_q), .clk(CLK), .clr(\复位 ));  // open: en
  assign controlled_buffer_5_out = controlled_buffer_21_out ? MDR_q : 8'bz;  // Controlled_Buffer controlled_buffer_23
  assign controlled_buffer_24_out = \手动  ? in_12 : 1'bz;  // Controlled_Buffer controlled_buffer_24
  assign controlled_buffer_21_out = not_1_out ? MDRo : 1'bz;  // Controlled_Buffer controlled_buffer_25
  assign controlled_buffer_24_out = not_1_out ? R0i : 1'bz;  // Controlled_Buffer controlled_buffer_26
  // Probe on R0i
  Decoder #(.select(2), .disabled(0)) decoder_2 (
    .out0(R0o), .out1(R1o), .out2(R2o), .out3(R3o), .sel(multiplexer_6_out), .en(rom_1_data[13]));
  assign controlled_buffer_27_out = controlled_buffer_24_out ? G_out : 8'bz;  // Controlled_Buffer controlled_buffer_27
  Register R0 (.D(controlled_buffer_27_out), .Q(R0_q), .clk(CLK), .clr(\复位 ));  // open: en
  assign controlled_buffer_5_out = controlled_buffer_30_out ? R0_q : 8'bz;  // Controlled_Buffer controlled_buffer_28
  assign controlled_buffer_29_out = \手动  ? in_14 : 1'bz;  // Controlled_Buffer controlled_buffer_29
  assign controlled_buffer_30_out = \手动  ? in_13 : 1'bz;  // Controlled_Buffer controlled_buffer_30
  assign controlled_buffer_30_out = not_1_out ? R0o : 1'bz;  // Controlled_Buffer controlled_buffer_31
  // Probe on R1i
  // Probe on R0o
  ROM #(.addrWidth(6), .dataWidth(24)) rom_1 (
    .addr(register_1_q),
    .data({IRi, IRo, PCi, PCo, PC_1, MARi, W_R, MDRi, MDRo, rom_1_data[14:13], Yi, Xi, ALUop, ALUo, G, rom_1_data[6:0]}));  // open: sel
  assign controlled_buffer_32_out = controlled_buffer_29_out ? G_out : 8'bz;  // Controlled_Buffer controlled_buffer_32
  Register R1 (.D(controlled_buffer_32_out), .Q(R1_q), .clk(CLK), .clr(\复位 ));  // open: en
  assign controlled_buffer_5_out = controlled_buffer_34_out ? R1_q : 8'bz;  // Controlled_Buffer controlled_buffer_33
  assign controlled_buffer_34_out = \手动  ? in_15 : 1'bz;  // Controlled_Buffer controlled_buffer_34
  assign controlled_buffer_29_out = not_1_out ? R1i : 1'bz;  // Controlled_Buffer controlled_buffer_35
  assign controlled_buffer_34_out = not_1_out ? R1o : 1'bz;  // Controlled_Buffer controlled_buffer_36
  // Probe on R1o
  assign controlled_buffer_37_out = controlled_buffer_39_out ? G_out : 8'bz;  // Controlled_Buffer controlled_buffer_37
  assign controlled_buffer_38_out = \手动  ? in_17 : 1'bz;  // Controlled_Buffer controlled_buffer_38
  assign controlled_buffer_39_out = \手动  ? in_16 : 1'bz;  // Controlled_Buffer controlled_buffer_39
  assign controlled_buffer_39_out = not_1_out ? R2i : 1'bz;  // Controlled_Buffer controlled_buffer_40
  assign controlled_buffer_38_out = not_1_out ? R2o : 1'bz;  // Controlled_Buffer controlled_buffer_41
  // Probe on R2i
  // Probe on R2o
  assign R3i_out = controlled_buffer_43_out ? G_out : 8'bz;  // Controlled_Buffer R3i
  Register R2 (.D(controlled_buffer_37_out), .Q(R2_q), .clk(CLK), .clr(\复位 ));  // open: en
  assign controlled_buffer_5_out = controlled_buffer_38_out ? R2_q : 8'bz;  // Controlled_Buffer controlled_buffer_42
  assign controlled_buffer_43_out = \手动  ? in_18 : 1'bz;  // Controlled_Buffer controlled_buffer_43
  assign controlled_buffer_44_out = \手动  ? in_19 : 1'bz;  // Controlled_Buffer controlled_buffer_44
  assign controlled_buffer_43_out = not_1_out ? R3i : 1'bz;  // Controlled_Buffer controlled_buffer_45
  // Probe on R3i
  Register R3 (.D(R3i_out), .Q(R3_q), .clk(CLK), .clr(\复位 ));  // open: en
  assign controlled_buffer_5_out = controlled_buffer_44_out ? R3_q : 8'bz;  // Controlled_Buffer controlled_buffer_46
  assign controlled_buffer_47_out = \手动  ? in_20 : 1'bz;  // Controlled_Buffer controlled_buffer_47
  assign controlled_buffer_44_out = not_1_out ? R3o : 1'bz;  // Controlled_Buffer controlled_buffer_48
  assign controlled_buffer_47_out = not_1_out ? Yi : 1'bz;  // Controlled_Buffer controlled_buffer_49
  // Probe on R3o
  // Probe on Yi
  assign controlled_buffer_50_out = controlled_buffer_47_out ? G_out : 8'bz;  // Controlled_Buffer controlled_buffer_50
  assign controlled_buffer_51_out = controlled_buffer_52_out ? G_out : 8'bz;  // Controlled_Buffer controlled_buffer_51
  assign controlled_buffer_52_out = \手动  ? in_21 : 1'bz;  // Controlled_Buffer controlled_buffer_52
  assign controlled_buffer_52_out = not_1_out ? Xi : 1'bz;  // Controlled_Buffer controlled_buffer_53
  // Probe on Xi
  Register A (.D(controlled_buffer_51_out), .Q(A_q), .clk(CLK), .clr(\复位 ));  // open: en
  Register B (.D(controlled_buffer_50_out), .Q(B_q), .clk(CLK), .clr(\复位 ));  // open: en
  assign controlled_buffer_54_out = \手动  ? in_22 : 2'bz;  // Controlled_Buffer controlled_buffer_54
  assign controlled_buffer_54_out = not_1_out ? ALUop : 2'bz;  // Controlled_Buffer controlled_buffer_55
  // Probe on ALUop
  // Probe on alu_1_aluresult
  ALU alu_1 (.A(A_q), .B(B_q), .ALUop(controlled_buffer_54_out), .ALUresult(alu_1_aluresult), .ZF(ZF));
  assign controlled_buffer_5_out = controlled_buffer_57_out ? alu_1_aluresult : 8'bz;  // Controlled_Buffer controlled_buffer_56
  assign controlled_buffer_57_out = \手动  ? in_23 : 1'bz;  // Controlled_Buffer controlled_buffer_57
  assign controlled_buffer_58_out = \手动  ? in_24 : 1'bz;  // Controlled_Buffer controlled_buffer_58
  assign controlled_buffer_57_out = not_1_out ? ALUo : 1'bz;  // Controlled_Buffer controlled_buffer_59
  // Probe on ALUo
  assign G_out = controlled_buffer_58_out ? controlled_buffer_5_out : 8'bz;  // Controlled_Buffer G
  assign controlled_buffer_58_out = not_1_out ? G : 1'bz;  // Controlled_Buffer controlled_buffer_60
  // Probe on G

  // Other names for the same wires on the sheet: RST = \复位 

  // Notes on the sheet:
  //   不同指令的微程序入口地址
  //   顺序执行
  //   手动输入控制信号
  //   存储器RAM
  //   微程序顺序-转移控制
  //   μPC
  //   控制存储器CM
  //   ADD
  //   SUB
  //   ST
  //   LD
  //   JE
  //   MOV
  //   ADDI
  //   contents of rom_1 (hex, n*v repeats v):
  //   1c0680 600 808680 400040 2e88 368c 4198 0 2e88 368c 4398 0 2e84 401680 40580 12680 20610 0 0 0 2e84
  //   401680 40580 600 c690 0 0 0 2e80 320 100e80 401680 200590 0 0 0 2e88 479c 0 0 2e84 401680 4594
  //   操作码3位,机器码8位 
  //    000,RB,RA,*
  //   001,RB,RA,*
  //   010,*****
  //   011,*****
  //   100,*****
  //   101,RB,RA,  (RA)->RB
  //   (RA)+(RB)->RA
  //   (RA)-(RB)->RA
  //   将R0里的内容存入内存(R1)+*****
  //   将内存地址（R1)+*****里内容给R0
  //   110 ，*****,将*****加到R1上
  //   判断R0内容是否为0，如果是0，则将PC更改为（PC)+1+*****
endmodule

module ALU (
  input  [7:0] A,
  input  [7:0] B,
  input  [1:0] ALUop,
  output [7:0] ALUresult,
  output ZF
);

  wire [7:0] adder_1_out, adder_2_out, bit_extender_1_out, subtractor_1_out;

  Adder adder_1 (.a(A), .b(B), .out(adder_1_out));  // open: cin, cout
  Subtractor subtractor_1 (.a(A), .b(B), .out(subtractor_1_out));  // open: bin, bout
  assign bit_extender_1_out = {{3{B[4]}}, B[4:0]};  // Bit_Extender bit_extender_1
  Comparator comparator_1 (.a(A), .b({8{1'b0}}), .eq(ZF));  // open: gt, lt
  Adder adder_2 (.a(A), .b(bit_extender_1_out), .out(adder_2_out));  // open: cin, cout
  Multiplexer #(.select(2), .width(8), .disabled(0), .enable("false")) multiplexer_1 (
    .in0(adder_1_out), .in1(subtractor_1_out), .in2(adder_2_out), .in3(A), .out(ALUresult), .sel(ALUop));

  // Notes on the sheet:
  //   ALUop,00A+B,01A-B.10A+立即数5位有符号扩展,11输出A
endmodule
