// Logisim project 浮点加法流水线实验.circ as structural Verilog: 4 circuits, main circuit main
module main (
  input  \A的符号 ,
  input  [7:0] \A的阶码 ,
  input  [22:0] \A的尾数 ,
  input  [22:0] \B的尾数 ,
  input  [7:0] \B的阶码 ,
  input  \B的符号 ,
  input  \启动 ,
  output \符号 ,
  output [7:0] \阶码 ,
  output [23:0] \尾数_包括隐藏位1_23位 ,
  output [22:0] out_11,
  output \溢出 
);

  wire decoder_1_out1, decoder_1_out2, decoder_1_out3, \对阶_1_a的尾数符号 , \对阶_1_b的尾数符号 , \尾数相加_1_尾数符号 , \时钟_out ;
  wire [1:0] multiplexer_1_out;
  wire [2:1] register_1_q;
  wire [7:0] \对阶_1_out_11 , \尾数相加_1_对阶后的阶码_2 ;
  wire [23:0] \对阶_1_对接后a尾数 , \对阶_1_对接后b尾数 ;
  wire [24:0] \尾数相加_1_尾数相加结果_25 ;

  Clock \u_时钟  (.out(\时钟_out ));
  // Probe on \对阶_1_对接后a尾数 
  // Probe on \对阶_1_out_11 
  // Probe on \对阶_1_a的尾数符号 
  \对阶  \u_对阶_1  (
    .A_Sign(\A的符号 ), .A_E(\A的阶码 ), .A_S(\A的尾数 ), .B_S(\B的尾数 ), .B_E(\B的阶码 ), .B_Sign(\B的符号 ),
    .\时钟 (\时钟_out ), .\触发器使能 (decoder_1_out1), .\A的尾数符号 (\对阶_1_a的尾数符号 ), .\对接后A尾数 (\对阶_1_对接后a尾数 ),
    .out_11(\对阶_1_out_11 ), .\对接后B尾数 (\对阶_1_对接后b尾数 ), .\B的尾数符号 (\对阶_1_b的尾数符号 ));
  // Probe on \对阶_1_b的尾数符号 
  \尾数相加  \u_尾数相加_1  (
    .\A的尾数符号 (\对阶_1_a的尾数符号 ), .\对阶后A的尾数 (\对阶_1_对接后a尾数 ), .\对阶后的阶码 (\对阶_1_out_11 ), .\对阶后B的尾数 (\对阶_1_对接后b尾数 ),
    .\B的尾数符号 (\对阶_1_b的尾数符号 ), .\时钟 (\时钟_out ), .\触发器使能 (decoder_1_out2), .\尾数符号 (\尾数相加_1_尾数符号 ),
    .\对阶后的阶码_2 (\尾数相加_1_对阶后的阶码_2 ), .\尾数相加结果_25 (\尾数相加_1_尾数相加结果_25 ));
  // Probe on \对阶_1_对接后b尾数 
  // Probe on \尾数相加_1_尾数符号 
  // Probe on \尾数相加_1_对阶后的阶码_2 
  // Probe on \尾数相加_1_尾数相加结果_25 
  \规格化  \u_规格化_1  (
    .\尾数符号 (\尾数相加_1_尾数符号 ), .\阶码 (\尾数相加_1_对阶后的阶码_2 ), .\尾数25位包括进位 (\尾数相加_1_尾数相加结果_25 ), .\时钟 (\时钟_out ),
    .\使能 (decoder_1_out3), .\尾数符号_2 (\符号 ), .\阶码_2 (\阶码 ), .\尾数包括隐藏位 ({\尾数_包括隐藏位1_23位 [23], out_11}),
    .\溢出 (\溢出 ));
  Decoder #(.select(2), .disabled(0), .enable("false")) decoder_1 (
    .out1(decoder_1_out1), .out2(decoder_1_out2), .out3(decoder_1_out3), .sel(register_1_q));  // open: out0
  Multiplexer #(.select(3), .width(2), .disabled(0), .enable("false")) multiplexer_1 (
    .in0(2'b00), .in1(2'b01), .in2(2'b00), .in3(2'b10), .in4(2'b00), .in5(2'b11), .in6(2'b00), .in7(2'b11),
    .out(multiplexer_1_out), .sel({register_1_q, \启动 }));
  // Probe on register_1_q
  Register #(.width(2)) register_1 (.D(multiplexer_1_out), .Q(register_1_q), .clk(\时钟_out ));  // open: en, clr

  assign \尾数_包括隐藏位1_23位 [22:0] = out_11;

  // Notes on the sheet:
  //   同上，输入B的单精度浮点数
  //   要想重新计算，请重复上述操作
  //   这里输入A的IEEE 754单精度浮点数，注意尾数23位，不包含隐藏的1
  //   对阶
  //   一开始时将启动设置为0，然后点击时钟一个周期，进入初始态00，再将启动设置为1，然后不断点击时钟观测结果
  //   在对阶阶段，小阶向大阶看齐
  //   相加
  //   规格化
  //            状态机
  //   初始态00:：启动为1次态01，启动0次态00
  //   对阶01:：启动为1次态10，启动0次态00
  //   加10：启动为1次态11，启动为0次态00
  //   规格化11：启动为1次态11，启动为0次态00
  //   尾数（23位置）
endmodule

module \对阶  (
  input  A_Sign,
  input  [7:0] A_E,
  input  [22:0] A_S,
  input  [22:0] B_S,
  input  [7:0] B_E,
  input  B_Sign,
  input  \时钟 ,
  input  \触发器使能 ,
  output \A的尾数符号 ,
  output [23:0] \对接后A尾数 ,
  output [7:0] out_11,
  output [23:0] \对接后B尾数 ,
  output \B的尾数符号 
);

  wire comparator_1_gt, comparator_1_lt, comparator_2_gt, comparator_3_gt;
  wire [4:0] multiplexer_1_out, multiplexer_2_out;
  wire [7:0] multiplexer_3_out, subtractor_1_out, subtractor_2_out;
  wire [7:5] multiplexer_1_out_2, multiplexer_2_out_2;
  wire [23:0] bit_extender_1_out, bit_extender_2_out, shifter_1_out, shifter_2_out;

  assign bit_extender_1_out = {{1{1'b1}}, A_S};  // Bit_Extender bit_extender_1
  assign bit_extender_2_out = {{1{1'b1}}, B_S};  // Bit_Extender bit_extender_2
  // Probe on bit_extender_2_out
  // Probe on subtractor_1_out
  Subtractor subtractor_1 (.a(B_E), .b(A_E), .out(subtractor_1_out));  // open: bin, bout
  Comparator #(.mode("unsigned")) comparator_1 (
    .a(A_E), .b(B_E), .gt(comparator_1_gt), .lt(comparator_1_lt));  // open: eq
  Subtractor subtractor_2 (.a(A_E), .b(B_E), .out(subtractor_2_out));  // open: bin, bout
  // Probe on subtractor_2_out
  // Probe on bit_extender_2_out
  // Probe on multiplexer_1_out
  Comparator #(.mode("unsigned")) comparator_2 (.a(subtractor_1_out), .b(8'h18), .gt(comparator_2_gt));  // open: eq, lt
  Comparator #(.mode("unsigned")) comparator_3 (.a(subtractor_2_out), .b(8'h18), .gt(comparator_3_gt));  // open: eq, lt
  // Probe on multiplexer_2_out
  Multiplexer #(.width(8), .disabled(0)) multiplexer_1 (
    .in0(subtractor_1_out), .in1(8'h18), .out({multiplexer_1_out_2, multiplexer_1_out}),
    .sel(comparator_2_gt), .en(comparator_1_lt));
  Multiplexer #(.width(8), .disabled(0)) multiplexer_2 (
    .in0(subtractor_2_out), .in1(8'h18), .out({multiplexer_2_out_2, multiplexer_2_out}),
    .sel(comparator_3_gt), .en(comparator_1_gt));
  Shifter #(.width(24), .shift("lr")) shifter_1 (
    .in(bit_extender_1_out), .\dist (multiplexer_1_out), .out(shifter_1_out));
  Shifter #(.width(24), .shift("lr")) shifter_2 (
    .in(bit_extender_2_out), .\dist (multiplexer_2_out), .out(shifter_2_out));
  Multiplexer #(.width(8), .disabled(0)) multiplexer_3 (
    .in0(A_E), .in1(B_E), .out(multiplexer_3_out), .sel(comparator_1_lt));  // open: en
  D_Flip_Flop d_ff_1 (.clk(\时钟 ), .D(A_Sign), .Q(\A的尾数符号 ), .en(\触发器使能 ));  // open: Qn, preset, reset
  Register #(.width(24)) register_1 (.D(shifter_1_out), .en(\触发器使能 ), .Q(\对接后A尾数 ), .clk(\时钟 ));  // open: clr
  Register register_2 (.D(multiplexer_3_out), .en(\触发器使能 ), .Q(out_11), .clk(\时钟 ));  // open: clr
  Register #(.width(24)) register_3 (.D(shifter_2_out), .en(\触发器使能 ), .Q(\对接后B尾数 ), .clk(\时钟 ));  // open: clr
  D_Flip_Flop d_ff_2 (.clk(\时钟 ), .D(B_Sign), .Q(\B的尾数符号 ), .en(\触发器使能 ));  // open: Qn, preset, reset

  // Notes on the sheet:
  //   对接后的阶码
endmodule

module \尾数相加  (
  input  \A的尾数符号 ,
  input  [23:0] \对阶后A的尾数 ,
  input  [7:0] \对阶后的阶码 ,
  input  [23:0] \对阶后B的尾数 ,
  input  \B的尾数符号 ,
  input  \时钟 ,
  input  \触发器使能 ,
  output \尾数符号 ,
  output [7:0] \对阶后的阶码_2 ,
  output [24:0] \尾数相加结果_25 
);

  wire multiplexer_3_out, xor_1_out;
  wire [2:2] comparator_1_lt;
  wire [24:0] adder_1_out, bit_extender_1_out, bit_extender_2_out, multiplexer_1_out, multiplexer_2_out,
       subtractor_1_out, subtractor_2_out;

  assign bit_extender_1_out = {{1{1'b0}}, \对阶后A的尾数 };  // Bit_Extender bit_extender_1
  assign bit_extender_2_out = {{1{1'b0}}, \对阶后B的尾数 };  // Bit_Extender bit_extender_2
  Adder #(.width(25)) adder_1 (.a(bit_extender_1_out), .b(bit_extender_2_out), .out(adder_1_out));  // open: cin, cout
  Subtractor #(.width(25)) subtractor_1 (
    .a(bit_extender_1_out), .b(bit_extender_2_out), .out(subtractor_1_out));  // open: bin, bout
  Subtractor #(.width(25)) subtractor_2 (
    .a(bit_extender_2_out), .b(bit_extender_1_out), .out(subtractor_2_out));  // open: bin, bout
  Comparator #(.width(25), .mode("unsigned")) comparator_1 (
    .a(bit_extender_1_out), .b(bit_extender_2_out), .lt(comparator_1_lt[2]));  // open: gt, eq
  Multiplexer #(.width(25), .disabled(0), .enable("false")) multiplexer_1 (
    .in0(subtractor_1_out), .in1(subtractor_2_out), .out(multiplexer_1_out), .sel(comparator_1_lt[2]));
  xor xor_1 (xor_1_out, \A的尾数符号 , \B的尾数符号 );
  Multiplexer #(.width(25), .disabled(0), .enable("false")) multiplexer_2 (
    .in0(adder_1_out), .in1(multiplexer_1_out), .out(multiplexer_2_out), .sel(xor_1_out));
  Multiplexer #(.select(3), .disabled(0), .enable("false")) multiplexer_3 (
    .in0(1'b0), .in1(1'b0), .in2(1'b1), .in3(1'b1), .in4(1'b0), .in5(1'b1), .in6(1'b0), .in7(1'b1),
    .out(multiplexer_3_out), .sel({comparator_1_lt[2], \A的尾数符号 , \B的尾数符号 }));
  Register register_1 (.D(\对阶后的阶码 ), .en(\触发器使能 ), .Q(\对阶后的阶码_2 ), .clk(\时钟 ));  // open: clr
  Register #(.width(25)) register_2 (.D(multiplexer_2_out), .en(\触发器使能 ), .Q(\尾数相加结果_25 ), .clk(\时钟 ));  // open: clr
  D_Flip_Flop d_ff_1 (.clk(\时钟 ), .D(multiplexer_3_out), .Q(\尾数符号 ), .en(\触发器使能 ));  // open: Qn, preset, reset
endmodule

module \规格化  (
  input  \尾数符号 ,
  input  [7:0] \阶码 ,
  input  [24:0] \尾数25位包括进位 ,
  input  \时钟 ,
  input  \使能 ,
  output \尾数符号_2 ,
  output [7:0] \阶码_2 ,
  output [23:0] \尾数包括隐藏位 ,
  output \溢出 
);

  wire adder_2_cout, comparator_1_eq, comparator_2_eq, multiplexer_6_out, multiplexer_9_out,
       priority_encoder_1_gs, priority_encoder_2_gs, priority_encoder_3_gs, priority_encoder_4_gs,
       subtractor_1_bout;
  wire [1:0] priority_encoder_4_out;
  wire [2:0] multiplexer_2_out, priority_encoder_1_out, priority_encoder_2_out, priority_encoder_3_out;
  wire [4:0] adder_3_out, multiplexer_4_out, subtractor_2_out;
  wire [7:0] adder_2_out, bit_extender_2_out, multiplexer_1_out, multiplexer_5_out, multiplexer_8_out,
       subtractor_1_out;
  wire [23:0] adder_1_out, bit_extender_1_out, multiplexer_3_out, multiplexer_7_out, shifter_2_out;
  wire [24:0] shifter_1_out;

  Comparator #(.width(24), .mode("unsigned")) comparator_1 (
    .a(\尾数25位包括进位 [23:0]), .b({24{1'b1}}), .eq(comparator_1_eq));  // open: gt, lt
  Priority_Encoder #(.disabled(0)) priority_encoder_1 (
    .in0(\尾数25位包括进位 [0]), .in1(\尾数25位包括进位 [1]), .in2(\尾数25位包括进位 [2]), .in3(\尾数25位包括进位 [3]),
    .in4(\尾数25位包括进位 [4]), .in5(\尾数25位包括进位 [5]), .in6(\尾数25位包括进位 [6]), .in7(\尾数25位包括进位 [7]),
    .out(priority_encoder_1_out), .gs(priority_encoder_1_gs));  // open: en_in, en_out
  Priority_Encoder #(.disabled(0)) priority_encoder_2 (
    .in0(\尾数25位包括进位 [8]), .in1(\尾数25位包括进位 [9]), .in2(\尾数25位包括进位 [10]), .in3(\尾数25位包括进位 [11]),
    .in4(\尾数25位包括进位 [12]), .in5(\尾数25位包括进位 [13]), .in6(\尾数25位包括进位 [14]), .in7(\尾数25位包括进位 [15]),
    .out(priority_encoder_2_out), .gs(priority_encoder_2_gs));  // open: en_in, en_out
  Priority_Encoder #(.disabled(0)) priority_encoder_3 (
    .in0(\尾数25位包括进位 [16]), .in1(\尾数25位包括进位 [17]), .in2(\尾数25位包括进位 [18]), .in3(\尾数25位包括进位 [19]),
    .in4(\尾数25位包括进位 [20]), .in5(\尾数25位包括进位 [21]), .in6(\尾数25位包括进位 [22]), .in7(\尾数25位包括进位 [23]),
    .out(priority_encoder_3_out), .gs(priority_encoder_3_gs));  // open: en_in, en_out
  Shifter #(.width(25), .shift("lr")) shifter_1 (.in(\尾数25位包括进位 ), .\dist (5'b00001), .out(shifter_1_out));
  Multiplexer #(.width(8), .disabled(0), .enable("false")) multiplexer_1 (
    .in0(8'h1), .in1(8'h2), .out(multiplexer_1_out), .sel(comparator_1_eq));
  // Probe on priority_encoder_1_out
  // Probe on priority_encoder_3_out
  assign bit_extender_1_out = {{23{1'b0}}, \尾数25位包括进位 [0]};  // Bit_Extender bit_extender_1
  Adder #(.width(24)) adder_1 (.a(shifter_1_out[23:0]), .b(bit_extender_1_out), .out(adder_1_out));  // open: cin, cout
  Adder adder_2 (.a(multiplexer_1_out), .b(\阶码 ), .out(adder_2_out), .cout(adder_2_cout));  // open: cin
  Priority_Encoder #(.select(2)) priority_encoder_4 (
    .in0(priority_encoder_1_gs), .in1(priority_encoder_2_gs), .in2(priority_encoder_3_gs),
    .out(priority_encoder_4_out), .gs(priority_encoder_4_gs));  // open: in3, en_out, en_in
  // Probe on priority_encoder_4_out
  Multiplexer #(.select(2), .width(3), .disabled(0), .enable("false")) multiplexer_2 (
    .in0(priority_encoder_1_out), .in1(priority_encoder_2_out), .in2(priority_encoder_3_out), .in3(3'b000),
    .out(multiplexer_2_out), .sel(priority_encoder_4_out));
  assign bit_extender_2_out = {{3{1'b0}}, subtractor_2_out};  // Bit_Extender bit_extender_2
  Multiplexer #(.width(24), .disabled(0), .enable("false")) multiplexer_3 (
    .in0(adder_1_out), .in1(24'h800000), .out(multiplexer_3_out), .sel(comparator_1_eq));
  Subtractor subtractor_1 (
    .a(\阶码 ), .b(bit_extender_2_out), .out(subtractor_1_out), .bout(subtractor_1_bout));  // open: bin
  Adder #(.width(5)) adder_3 (
    .a({priority_encoder_4_out, multiplexer_2_out}), .b(5'b00001), .out(adder_3_out));  // open: cin, cout
  Multiplexer #(.width(5), .disabled(0), .enable("false")) multiplexer_4 (
    .in0({5{1'b0}}), .in1(adder_3_out), .out(multiplexer_4_out), .sel(priority_encoder_4_gs));
  // Probe on multiplexer_4_out
  Subtractor #(.width(5)) subtractor_2 (
    .a(5'b11000), .b(multiplexer_4_out), .out(subtractor_2_out));  // open: bin, bout
  // Probe on subtractor_2_out
  Multiplexer #(.width(8), .disabled(0), .enable("false")) multiplexer_5 (
    .in0(subtractor_1_out), .in1(adder_2_out), .out(multiplexer_5_out), .sel(\尾数25位包括进位 [24]));
  Multiplexer #(.disabled(0), .enable("false")) multiplexer_6 (
    .in0(subtractor_1_bout), .in1(adder_2_cout), .out(multiplexer_6_out), .sel(\尾数25位包括进位 [24]));
  Shifter #(.width(24)) shifter_2 (.in(\尾数25位包括进位 [23:0]), .\dist (subtractor_2_out), .out(shifter_2_out));
  Multiplexer #(.width(24), .disabled(0), .enable("false")) multiplexer_7 (
    .in0(shifter_2_out), .in1(multiplexer_3_out), .out(multiplexer_7_out), .sel(\尾数25位包括进位 [24]));
  Comparator #(.width(24), .mode("unsigned")) comparator_2 (
    .a(multiplexer_7_out), .b({24{1'b0}}), .eq(comparator_2_eq));  // open: gt, lt
  Multiplexer #(.width(8), .disabled(0), .enable("false")) multiplexer_8 (
    .in0(multiplexer_5_out), .in1({8{1'b0}}), .out(multiplexer_8_out), .sel(comparator_2_eq));
  Multiplexer #(.disabled(0), .enable("false")) multiplexer_9 (
    .in0(\尾数符号 ), .in1(1'b0), .out(multiplexer_9_out), .sel(comparator_2_eq));
  Register register_1 (.D(multiplexer_8_out), .en(\使能 ), .Q(\阶码_2 ), .clk(\时钟 ));  // open: clr
  Register #(.width(24)) register_2 (.D(multiplexer_7_out), .en(\使能 ), .Q(\尾数包括隐藏位 ), .clk(\时钟 ));  // open: clr
  Register #(.width(1)) register_3 (.D(multiplexer_9_out), .en(\使能 ), .Q(\尾数符号_2 ), .clk(\时钟 ));  // open: clr
  Register #(.width(1)) register_4 (.D(multiplexer_6_out), .en(\使能 ), .Q(\溢出 ), .clk(\时钟 ));  // open: clr

  // Notes on the sheet:
  //   这一部分是确定（隐藏位+尾数）出现1的最位
endmodule
