// Logisim project 海明码实验.circ as structural Verilog: 3 circuits, main circuit main
module main (
  input  M1,
  input  M2,
  input  M3,
  input  M4,
  input  M5,
  input  M6,
  input  M7,
  input  M8,
  input  P1_star,
  input  P2_star,
  input  M1_star,
  input  P3_star,
  input  M2_star,
  input  M3_star,
  input  M4_2,
  input  P4_star,
  input  M5_star,
  input  M6_star,
  input  M7_star,
  input  M8_star,
  output S1,
  output S2,
  output S3,
  output P1,
  output P2,
  output M1_2,
  output P3,
  output M2_2,
  output M3_2,
  output M4_3,
  output P4,
  output M5_2,
  output M6_2,
  output M7_2,
  output M8_2,
  output S4,
  output out_37,
  output out_38,
  output M1_3,
  output out_40,
  output M2_3,
  output M3_3,
  output M4_4,
  output P4_2,
  output M5_3,
  output M6_3,
  output M7_3,
  output M8_3
);

  wire decoder_1_out1, decoder_1_out2, decoder_1_out3, decoder_1_out4, decoder_1_out5, decoder_1_out6,
       decoder_1_out7, decoder_1_out8, decoder_1_out9, decoder_1_out10, decoder_1_out11, decoder_1_out12,
       xor4_3_out_5, xor4_4_out_5, xor5_3_out_6, xor5_4_out_6;

  XOR5 xor5_1 (.in_1(M1), .in_2(M2), .in_3(M4), .in_4(M5), .in_5(M7), .out_6(P1));
  XOR5 xor5_2 (.in_1(M1), .in_2(M3), .in_3(M4), .in_4(M6), .in_5(M7), .out_6(P2));
  XOR4 xor4_1 (.in_1(M2), .in_2(M3), .in_3(M4), .in_4(M8), .out_5(P3));
  XOR4 xor4_2 (.in_1(M5), .in_2(M6), .in_3(M7), .in_4(M8), .out_5(P4));
  xor xor_1 (out_37, P1_star, decoder_1_out1);
  xor xor_2 (out_38, P2_star, decoder_1_out2);
  xor xor_3 (M1_3, M1_star, decoder_1_out3);
  xor xor_4 (out_40, P3_star, decoder_1_out4);
  xor xor_5 (M2_3, M2_star, decoder_1_out5);
  xor xor_6 (M3_3, M3_star, decoder_1_out6);
  xor xor_7 (P4_2, P4_star, decoder_1_out8);
  xor xor_8 (M5_3, M5_star, decoder_1_out9);
  xor xor_9 (M4_4, M4_2, decoder_1_out7);
  xor xor_10 (M7_3, M7_star, decoder_1_out11);
  xor xor_11 (M6_3, M6_star, decoder_1_out10);
  xor xor_12 (M8_3, M8_star, decoder_1_out12);
  XOR5 xor5_3 (.in_1(M1_star), .in_2(M2_star), .in_3(M4_2), .in_4(M5_star), .in_5(M7_star), .out_6(xor5_3_out_6));
  XOR5 xor5_4 (.in_1(M1_star), .in_2(M3_star), .in_3(M4_2), .in_4(M6_star), .in_5(M7_star), .out_6(xor5_4_out_6));
  XOR4 xor4_3 (.in_1(M2_star), .in_2(M3_star), .in_3(M4_2), .in_4(M8_star), .out_5(xor4_3_out_5));
  XOR4 xor4_4 (.in_1(M5_star), .in_2(M6_star), .in_3(M7_star), .in_4(M8_star), .out_5(xor4_4_out_5));
  xor xor_13 (S1, xor5_3_out_6, P1_star);
  xor xor_14 (S2, xor5_4_out_6, P2_star);
  xor xor_15 (S3, xor4_3_out_5, P3_star);
  xor xor_16 (S4, xor4_4_out_5, P4_star);
  Decoder #(.select(4), .disabled(0), .enable("false")) decoder_1 (
    .out1(decoder_1_out1), .out2(decoder_1_out2), .out3(decoder_1_out3), .out4(decoder_1_out4),
    .out5(decoder_1_out5), .out6(decoder_1_out6), .out7(decoder_1_out7), .out8(decoder_1_out8),
    .out9(decoder_1_out9), .out10(decoder_1_out10), .out11(decoder_1_out11), .out12(decoder_1_out12),
    .sel({S4, S3, S2, S1}));  // open: out0, out13, out14, out15

  assign M1_2 = M1;
  assign M2_2 = M2;
  assign M3_2 = M3;
  assign M4_3 = M4;
  assign M5_2 = M5;
  assign M6_2 = M6;
  assign M7_2 = M7;
  assign M8_2 = M8;

  // Notes on the sheet:
  //   8位信息位，所以校验位要4位
  //   海明码生成电路
  //   XOR5
  //   XOR4
  //   XOR4
  //   生成的海明码
  //   P1
  //   P2
  //   P3
  //   P4
  //   （注，将左边生成的海明码修改1位变成1位出错的海明码）
  //   位置
  //   接收到的海明码中的信息位
  //   1
  //   修改后的码
  //   P1
  //   2
  //   4
  //   3
  //   P2
  //   P3
  //   5
  //   6
  //   7
  //   9
  //   8
  //   *
  //   11
  //   10
  //   12
  //   XOR5
  //   XOR4
  //   XOR4
  //   S4S3S2S1=0000, 表示没有出错，S4S3S2S1=0001表示P1*出错，S4S3S2S1=1100(12)表示M8*出错
  //   P1**
  //   P2**
  //   P3**
  //   P4**
  //   将要修改的位与1做异或（即非运算）
  //   根据S4S3S2S1定位接收到海明码哪里出错了
  //   这是译码器最多1个输出为1
  //   输出为1的表明对应的位出错了
  //   如果都输出为0，则表示没有出错的
endmodule

module XOR4 (
  input  in_1,
  input  in_2,
  input  in_3,
  input  in_4,
  output out_5
);

  wire xor_1_out, xor_2_out;

  xor xor_1 (xor_1_out, in_1, in_2);
  xor xor_2 (xor_2_out, in_3, in_4);
  xor xor_3 (out_5, xor_1_out, xor_2_out);
endmodule

module XOR5 (
  input  in_1,
  input  in_2,
  input  in_3,
  input  in_4,
  input  in_5,
  output out_6
);

  wire xor_1_out, xor_2_out, xor_3_out;

  xor xor_1 (xor_1_out, in_1, in_2);
  xor xor_2 (xor_2_out, in_4, in_5);
  xor xor_3 (xor_3_out, xor_1_out, in_3);
  xor xor_4 (out_6, xor_3_out, xor_2_out);
endmodule
