// Logisim project 补码加减运算以及溢出判断实验.circ as structural Verilog: 1 circuit, main circuit main
module main (
  input  [2:0] \A的补码 ,
  input  [2:0] \B的补码 ,
  input  \_1为减 ,
  output \_1表示结果为正数 ,
  output \_1表示出现下溢出 ,
  output \_1表示是负数 ,
  output out_7,
  output [2:0] out_8
);

  wire [3:0] bit_extender_1_out, bit_extender_2_out, xor_4_out;
  wire [3:3] adder_1_out;

  assign bit_extender_1_out = {{1{\A的补码 [2]}}, \A的补码 };  // Bit_Extender bit_extender_1
  assign bit_extender_2_out = {{1{\B的补码 [2]}}, \B的补码 };  // Bit_Extender bit_extender_2
  // Probe on bit_extender_1_out
  // Probe on bit_extender_2_out
  xor xor_1 (xor_4_out[3], \_1为减 , bit_extender_2_out[3]);
  xor xor_2 (xor_4_out[2], \_1为减 , bit_extender_2_out[2]);
  xor xor_3 (xor_4_out[1], \_1为减 , bit_extender_2_out[1]);
  xor xor_4 (xor_4_out[0], \_1为减 , bit_extender_2_out[0]);
  Adder #(.width(4)) adder_1 (
    .a(bit_extender_1_out), .b(xor_4_out), .out({adder_1_out[3], out_8}), .cin(\_1为减 ));  // open: cout
  // Probe on {adder_1_out[3], out_8}
  Decoder #(.select(2), .disabled(0), .enable("false")) decoder_1 (
    .out0(\_1表示结果为正数 ), .out1(\_1表示出现下溢出 ), .out2(\_1表示是负数 ), .out3(out_7), .sel({adder_1_out[3], out_8[2]}));

  // Notes on the sheet:
  //   补码加减法器
  //   有符号位扩展
  //   0为加
  //   实现A补+B补, A补+（-B)补
  //   A的变形补码
  //   运算时A和B的补码采用变形补码
  //   根据符号位（最高两位）判断是否有溢出以及类型
  //   1表示出现上溢出
endmodule
