// Logisim project 运算器和寄存器以及译码实验.circ as structural Verilog: 2 circuits, main circuit main
module main (
  input  [1:0] \源寄存器A ,
  input  [2:0] \操作码 ,
  input  [1:0] \目的寄存器 ,
  input  [1:0] \源寄存器B ,
  output [7:0] out_5,
  output [7:0] out_6
);

  wire clock_1_out, decoder_1_out0, decoder_1_out1, decoder_1_out2, decoder_1_out3;
  wire [7:0] alu_1_out_4, R0_q, R1_q, R2_q, R3_q;

  Clock clock_1 (.out(clock_1_out));
  Decoder #(.select(2), .disabled(0), .enable("false")) decoder_1 (
    .out0(decoder_1_out0), .out1(decoder_1_out1), .out2(decoder_1_out2), .out3(decoder_1_out3), .sel(\目的寄存器 ));
  Register R0 (.D(alu_1_out_4), .en(decoder_1_out0), .Q(R0_q), .clk(clock_1_out));  // open: clr
  Register R1 (.D(alu_1_out_4), .en(decoder_1_out1), .Q(R1_q), .clk(clock_1_out));  // open: clr
  Register R2 (.D(alu_1_out_4), .en(decoder_1_out2), .Q(R2_q), .clk(clock_1_out));  // open: clr
  Register R3 (.D(alu_1_out_4), .en(decoder_1_out3), .Q(R3_q), .clk(clock_1_out));  // open: clr
  Multiplexer #(.select(2), .width(8), .disabled(0), .enable("false")) multiplexer_1 (
    .in0(R0_q), .in1(R1_q), .in2(R2_q), .in3(R3_q), .out(out_5), .sel(\源寄存器A ));
  Multiplexer #(.select(2), .width(8), .disabled(0), .enable("false")) multiplexer_2 (
    .in0(R0_q), .in1(R1_q), .in2(R2_q), .in3(R3_q), .out(out_6), .sel(\源寄存器B ));
  ALU alu_1 (.aluop(\操作码 ), .A(out_5), .B(out_6), .out_4(alu_1_out_4));
  // Probe on alu_1_out_4

  // Notes on the sheet:
  //   read-A ctrl
  //   read-B ctrl
  //   read-A ctrl
  //   控制端和输出
  //   000，A
  //   001，A+B
  //   010，A-B
  //   011，A<<B
  //   100，A>>B
  //   101，A*B
  //   111，A|B
  //   110,A&B
endmodule

module ALU (
  input  [2:0] aluop,
  input  [7:0] A,
  input  [7:0] B,
  output [7:0] out_4
);

  wire [7:0] adder_1_out, and_1_out, multiplier_1_out, or_1_out, shifter_1_out, shifter_2_out,
       subtractor_1_out;

  Adder adder_1 (.a(A), .b(B), .out(adder_1_out));  // open: cin, cout
  Subtractor subtractor_1 (.a(A), .b(B), .out(subtractor_1_out));  // open: bin, bout
  Shifter shifter_1 (.in(A), .\dist (B[2:0]), .out(shifter_1_out));
  Shifter #(.shift("lr")) shifter_2 (.in(A), .\dist (B[2:0]), .out(shifter_2_out));
  Multiplier multiplier_1 (.a(A), .b(B), .out(multiplier_1_out));  // open: cin, cout
  assign and_1_out = A & B;  // AND_Gate and_1, 8 bits wide
  assign or_1_out = A | B;  // OR_Gate or_1, 8 bits wide
  Multiplexer #(.select(3), .width(8), .disabled(0), .enable("false")) multiplexer_1 (
    .in0(A), .in1(adder_1_out), .in2(subtractor_1_out), .in3(shifter_1_out), .in4(shifter_2_out),
    .in5(multiplier_1_out), .in6(and_1_out), .in7(or_1_out), .out(out_4), .sel(aluop));

  // Notes on the sheet:
  //   控制端和输出
  //   000，A
  //   010，A-B
  //   011，A<<B
  //   100，A>>B
  //   111，A|B
  //   001，A+B
  //   101，A*B
  //   110,A&B
endmodule
